// Logisim project testassignment1.circ as structural Verilog: 1 circuit, main circuit main
module main (
  input  in_1,
  input  in_2,
  input  in_3,
  input  in_4,
  input  in_5,
  input  in_6,
  input  in_7,
  input  in_8,
  input  in_9,
  input  in_10,
  input  in_11,
  input  in_12
);

  wire and_1_out, and_2_out, and_3_out, and_4_out, and_5_out, and_6_out, and_7_out, and_8_out, and_9_out,
       and_10_out, and_11_out, and_12_out, and_13_out, and_14_out, and_15_out, and_16_out, and_17_out,
       and_18_out, clock_1_out, clock_2_out, d_ff_2_q, d_ff_9_q, d_ff_10_q, d_ff_17_q, d_ff_24_q, d_ff_25_q,
       j_k_ff_1_q, j_k_ff_2_q, j_k_ff_3_q, j_k_ff_4_q, j_k_ff_5_q, j_k_ff_6_q, j_k_ff_7_q, j_k_ff_8_q,
       j_k_ff_9_q, j_k_ff_10_q, j_k_ff_11_q, j_k_ff_12_q, j_k_ff_13_q, j_k_ff_14_q, j_k_ff_15_q, j_k_ff_16_q,
       j_k_ff_17_q, j_k_ff_18_q, j_k_ff_19_q, j_k_ff_20_q, j_k_ff_21_q, j_k_ff_22_q, j_k_ff_23_q,
       j_k_ff_24_q, j_k_ff_25_q, j_k_ff_26_q, nand_1_out, nand_2_out;
  wire [1:0] d_ff_12_q, d_ff_19_q;
  wire [2:0] d_ff_5_q, d_ff_29_q;
  wire [3:0] d_ff_1_q, d_ff_11_q, d_ff_18_q, d_ff_26_q;

  Clock clock_1 (.out(clock_1_out));
  J_K_Flip_Flop j_k_ff_1 (
    .J(in_2), .K(in_2), .clk(clock_1_out), .Q(j_k_ff_1_q), .reset(and_4_out));  // open: Qn, preset
  D_Flip_Flop d_ff_1 (.D(j_k_ff_1_q), .clk(clock_1_out), .Q(d_ff_1_q[0]));  // open: Qn, preset, reset
  D_Flip_Flop d_ff_2 (.D(j_k_ff_6_q), .clk(clock_1_out), .Q(d_ff_2_q));  // open: Qn, preset, reset
  LED led_1 (.in(j_k_ff_1_q));
  J_K_Flip_Flop j_k_ff_2 (
    .J(j_k_ff_1_q), .K(j_k_ff_1_q), .clk(clock_1_out), .Q(j_k_ff_2_q), .reset(and_4_out));  // open: Qn, preset
  D_Flip_Flop d_ff_3 (.D(j_k_ff_2_q), .clk(clock_1_out), .Q(d_ff_1_q[1]));  // open: Qn, preset, reset
  J_K_Flip_Flop j_k_ff_3 (.J(in_5), .K(in_5), .clk(d_ff_2_q), .Q(j_k_ff_3_q), .reset(and_5_out));  // open: Qn, preset
  LED led_2 (.in(j_k_ff_3_q));
  and and_1 (and_1_out, j_k_ff_1_q, j_k_ff_2_q);
  J_K_Flip_Flop j_k_ff_4 (
    .J(and_1_out), .K(and_1_out), .clk(clock_1_out), .Q(j_k_ff_4_q), .reset(and_4_out));  // open: Qn, preset
  LED led_3 (.in(j_k_ff_2_q));
  D_Flip_Flop d_ff_4 (.D(j_k_ff_4_q), .clk(clock_1_out), .Q(d_ff_1_q[2]));  // open: Qn, preset, reset
  J_K_Flip_Flop j_k_ff_5 (
    .J(j_k_ff_3_q), .K(j_k_ff_3_q), .clk(d_ff_2_q), .Q(j_k_ff_5_q), .reset(and_5_out));  // open: Qn, preset
  D_Flip_Flop #(.trigger("falling")) d_ff_5 (
    .D(j_k_ff_3_q), .clk(d_ff_2_q), .Q(d_ff_5_q[0]));  // open: Qn, preset, reset
  LED led_4 (.in(j_k_ff_4_q));
  LED led_5 (.in(j_k_ff_5_q));
  and and_2 (and_2_out, and_1_out, j_k_ff_4_q);
  J_K_Flip_Flop j_k_ff_6 (
    .J(and_2_out), .K(and_2_out), .clk(clock_1_out), .Q(j_k_ff_6_q), .reset(and_4_out));  // open: Qn, preset
  D_Flip_Flop d_ff_6 (.D(j_k_ff_6_q), .clk(clock_1_out), .Q(d_ff_1_q[3]));  // open: Qn, preset, reset
  and and_3 (and_3_out, j_k_ff_3_q, j_k_ff_5_q);
  J_K_Flip_Flop j_k_ff_7 (
    .J(and_3_out), .K(and_3_out), .clk(d_ff_2_q), .Q(j_k_ff_7_q), .reset(and_5_out));  // open: Qn, preset
  D_Flip_Flop #(.trigger("falling")) d_ff_7 (
    .D(j_k_ff_5_q), .clk(d_ff_2_q), .Q(d_ff_5_q[1]));  // open: Qn, preset, reset
  LED led_6 (.in(j_k_ff_6_q));
  LED led_7 (.in(j_k_ff_7_q));
  D_Flip_Flop #(.trigger("falling")) d_ff_8 (
    .D(j_k_ff_7_q), .clk(d_ff_2_q), .Q(d_ff_5_q[2]));  // open: Qn, preset, reset
  and and_4 (and_4_out, j_k_ff_2_q, j_k_ff_6_q);
  and and_5 (and_5_out, j_k_ff_7_q, j_k_ff_5_q);
  Hex_Digit_Display hex_digit_display_1 (.value({{2{in_3}}, d_ff_12_q}));  // open: dp
  Hex_Digit_Display hex_digit_display_2 (.value(d_ff_11_q));  // open: dp
  Hex_Digit_Display hex_digit_display_3 (.value({in_6, d_ff_5_q}));  // open: dp
  Hex_Digit_Display hex_digit_display_4 (.value(d_ff_1_q));  // open: dp
  D_Flip_Flop d_ff_9 (.D(j_k_ff_9_q), .clk(nand_1_out), .Q(d_ff_9_q));  // open: Qn, preset, reset
  D_Flip_Flop d_ff_10 (.D(j_k_ff_7_q), .clk(d_ff_2_q), .Q(d_ff_10_q));  // open: Qn, preset, reset
  J_K_Flip_Flop j_k_ff_8 (.J(in_4), .K(in_4), .clk(nand_1_out), .Q(j_k_ff_8_q), .reset(and_9_out));  // open: Qn, preset
  D_Flip_Flop d_ff_11 (.D(j_k_ff_8_q), .clk(nand_1_out), .Q(d_ff_11_q[0]));  // open: Qn, preset, reset
  J_K_Flip_Flop j_k_ff_9 (
    .J(in_1), .K(in_1), .clk(j_k_ff_13_q), .Q(j_k_ff_9_q), .reset(and_7_out));  // open: Qn, preset
  D_Flip_Flop d_ff_12 (.D(j_k_ff_9_q), .clk(d_ff_9_q), .Q(d_ff_12_q[0]));  // open: Qn, preset, reset
  LED led_8 (.in(j_k_ff_8_q));
  nand nand_1 (nand_1_out, j_k_ff_7_q, d_ff_10_q);
  J_K_Flip_Flop j_k_ff_10 (
    .J(j_k_ff_9_q), .K(j_k_ff_9_q), .clk(j_k_ff_13_q), .Q(j_k_ff_10_q), .reset(and_7_out));  // open: Qn, preset
  LED led_9 (.in(j_k_ff_9_q));
  D_Flip_Flop d_ff_13 (.D(j_k_ff_10_q), .clk(d_ff_9_q), .Q(d_ff_12_q[1]));  // open: Qn, preset, reset
  J_K_Flip_Flop j_k_ff_11 (
    .J(j_k_ff_8_q), .K(j_k_ff_8_q), .clk(nand_1_out), .Q(j_k_ff_11_q), .reset(and_9_out));  // open: Qn, preset
  D_Flip_Flop d_ff_14 (.D(j_k_ff_11_q), .clk(nand_1_out), .Q(d_ff_11_q[1]));  // open: Qn, preset, reset
  LED led_10 (.in(j_k_ff_10_q));
  and and_6 (and_6_out, j_k_ff_8_q, j_k_ff_11_q);
  J_K_Flip_Flop j_k_ff_12 (
    .J(and_6_out), .K(and_6_out), .clk(nand_1_out), .Q(j_k_ff_12_q), .reset(and_9_out));  // open: Qn, preset
  LED led_11 (.in(j_k_ff_11_q));
  D_Flip_Flop d_ff_15 (.D(j_k_ff_12_q), .clk(nand_1_out), .Q(d_ff_11_q[2]));  // open: Qn, preset, reset
  and and_7 (and_7_out, j_k_ff_9_q, j_k_ff_10_q);
  LED led_12 (.in(j_k_ff_12_q));
  and and_8 (and_8_out, and_6_out, j_k_ff_12_q);
  J_K_Flip_Flop j_k_ff_13 (
    .J(and_8_out), .K(and_8_out), .clk(nand_1_out), .Q(j_k_ff_13_q), .reset(and_9_out));  // open: Qn, preset
  D_Flip_Flop d_ff_16 (.D(j_k_ff_13_q), .clk(nand_1_out), .Q(d_ff_11_q[3]));  // open: Qn, preset, reset
  LED led_13 (.in(j_k_ff_13_q));
  and and_9 (and_9_out, j_k_ff_11_q, j_k_ff_13_q);
  D_Flip_Flop d_ff_17 (.D(j_k_ff_14_q), .clk(nand_2_out), .Q(d_ff_17_q));  // open: Qn, preset, reset
  J_K_Flip_Flop j_k_ff_14 (
    .J(in_8), .K(in_8), .clk(j_k_ff_19_q), .Q(j_k_ff_14_q), .reset(and_10_out));  // open: Qn, preset
  J_K_Flip_Flop j_k_ff_15 (
    .J(in_10), .K(in_10), .clk(nand_2_out), .Q(j_k_ff_15_q), .reset(and_13_out));  // open: Qn, preset
  LED led_14 (.in(j_k_ff_15_q));
  D_Flip_Flop d_ff_18 (.D(j_k_ff_15_q), .clk(nand_2_out), .Q(d_ff_18_q[0]));  // open: Qn, preset, reset
  LED led_15 (.in(j_k_ff_14_q));
  D_Flip_Flop d_ff_19 (.D(j_k_ff_14_q), .clk(d_ff_17_q), .Q(d_ff_19_q[0]));  // open: Qn, preset, reset
  J_K_Flip_Flop j_k_ff_16 (
    .J(j_k_ff_15_q), .K(j_k_ff_15_q), .clk(nand_2_out), .Q(j_k_ff_16_q), .reset(and_13_out));  // open: Qn, preset
  D_Flip_Flop d_ff_20 (.D(j_k_ff_16_q), .clk(nand_2_out), .Q(d_ff_18_q[1]));  // open: Qn, preset, reset
  J_K_Flip_Flop j_k_ff_17 (
    .J(j_k_ff_14_q), .K(j_k_ff_14_q), .clk(j_k_ff_19_q), .Q(j_k_ff_17_q), .reset(and_10_out));  // open: Qn, preset
  D_Flip_Flop d_ff_21 (.D(j_k_ff_17_q), .clk(d_ff_17_q), .Q(d_ff_19_q[1]));  // open: Qn, preset, reset
  LED led_16 (.in(j_k_ff_16_q));
  and and_10 (and_10_out, j_k_ff_14_q, j_k_ff_17_q);
  LED led_17 (.in(j_k_ff_17_q));
  and and_11 (and_11_out, j_k_ff_15_q, j_k_ff_16_q);
  J_K_Flip_Flop j_k_ff_18 (
    .J(and_11_out), .K(and_11_out), .clk(nand_2_out), .Q(j_k_ff_18_q), .reset(and_13_out));  // open: Qn, preset
  LED led_18 (.in(j_k_ff_18_q));
  D_Flip_Flop d_ff_22 (.D(j_k_ff_18_q), .clk(nand_2_out), .Q(d_ff_18_q[2]));  // open: Qn, preset, reset
  and and_12 (and_12_out, and_11_out, j_k_ff_18_q);
  J_K_Flip_Flop j_k_ff_19 (
    .J(and_12_out), .K(and_12_out), .clk(nand_2_out), .Q(j_k_ff_19_q), .reset(and_13_out));  // open: Qn, preset
  D_Flip_Flop d_ff_23 (.D(j_k_ff_19_q), .clk(nand_2_out), .Q(d_ff_18_q[3]));  // open: Qn, preset, reset
  LED led_19 (.in(j_k_ff_19_q));
  and and_13 (and_13_out, j_k_ff_16_q, j_k_ff_19_q);
  nand nand_2 (nand_2_out, d_ff_24_q, j_k_ff_26_q);
  D_Flip_Flop d_ff_24 (.D(j_k_ff_26_q), .clk(d_ff_25_q), .Q(d_ff_24_q));  // open: Qn, preset, reset
  Clock clock_2 (.out(clock_2_out));
  Hex_Digit_Display hex_digit_display_5 (.value({{2{in_9}}, d_ff_19_q}));  // open: dp
  Hex_Digit_Display hex_digit_display_6 (.value(d_ff_18_q));  // open: dp
  J_K_Flip_Flop j_k_ff_20 (
    .J(in_7), .K(in_7), .clk(clock_2_out), .Q(j_k_ff_20_q), .reset(and_17_out));  // open: Qn, preset
  D_Flip_Flop d_ff_25 (.D(j_k_ff_25_q), .clk(clock_2_out), .Q(d_ff_25_q));  // open: Qn, preset, reset
  Hex_Digit_Display hex_digit_display_7 (.value({in_12, d_ff_29_q}));  // open: dp
  Hex_Digit_Display hex_digit_display_8 (.value(d_ff_26_q));  // open: dp
  LED led_20 (.in(j_k_ff_20_q));
  D_Flip_Flop d_ff_26 (.D(j_k_ff_20_q), .clk(clock_2_out), .Q(d_ff_26_q[0]));  // open: Qn, preset, reset
  J_K_Flip_Flop j_k_ff_21 (
    .J(j_k_ff_20_q), .K(j_k_ff_20_q), .clk(clock_2_out), .Q(j_k_ff_21_q), .reset(and_17_out));  // open: Qn, preset
  D_Flip_Flop d_ff_27 (.D(j_k_ff_21_q), .clk(clock_2_out), .Q(d_ff_26_q[1]));  // open: Qn, preset, reset
  J_K_Flip_Flop j_k_ff_22 (
    .J(in_11), .K(in_11), .clk(d_ff_25_q), .Q(j_k_ff_22_q), .reset(and_18_out));  // open: Qn, preset
  J_K_Flip_Flop j_k_ff_23 (
    .J(and_14_out), .K(and_14_out), .clk(clock_2_out), .Q(j_k_ff_23_q), .reset(and_17_out));  // open: Qn, preset
  LED led_21 (.in(j_k_ff_21_q));
  D_Flip_Flop d_ff_28 (.D(j_k_ff_23_q), .clk(clock_2_out), .Q(d_ff_26_q[2]));  // open: Qn, preset, reset
  J_K_Flip_Flop j_k_ff_24 (
    .J(j_k_ff_22_q), .K(j_k_ff_22_q), .clk(d_ff_25_q), .Q(j_k_ff_24_q), .reset(and_18_out));  // open: Qn, preset
  LED led_22 (.in(j_k_ff_22_q));
  D_Flip_Flop #(.trigger("falling")) d_ff_29 (
    .D(j_k_ff_22_q), .clk(d_ff_25_q), .Q(d_ff_29_q[0]));  // open: Qn, preset, reset
  and and_14 (and_14_out, j_k_ff_20_q, j_k_ff_21_q);
  LED led_23 (.in(j_k_ff_23_q));
  LED led_24 (.in(j_k_ff_24_q));
  and and_15 (and_15_out, and_14_out, j_k_ff_23_q);
  J_K_Flip_Flop j_k_ff_25 (
    .J(and_15_out), .K(and_15_out), .clk(clock_2_out), .Q(j_k_ff_25_q), .reset(and_17_out));  // open: Qn, preset
  D_Flip_Flop d_ff_30 (.D(j_k_ff_25_q), .clk(clock_2_out), .Q(d_ff_26_q[3]));  // open: Qn, preset, reset
  and and_16 (and_16_out, j_k_ff_22_q, j_k_ff_24_q);
  J_K_Flip_Flop j_k_ff_26 (
    .J(and_16_out), .K(and_16_out), .clk(d_ff_25_q), .Q(j_k_ff_26_q), .reset(and_18_out));  // open: Qn, preset
  D_Flip_Flop #(.trigger("falling")) d_ff_31 (
    .D(j_k_ff_24_q), .clk(d_ff_25_q), .Q(d_ff_29_q[1]));  // open: Qn, preset, reset
  LED led_25 (.in(j_k_ff_25_q));
  LED led_26 (.in(j_k_ff_26_q));
  and and_17 (and_17_out, j_k_ff_21_q, j_k_ff_25_q);
  and and_18 (and_18_out, j_k_ff_26_q, j_k_ff_24_q);
  D_Flip_Flop #(.trigger("falling")) d_ff_32 (
    .D(j_k_ff_26_q), .clk(d_ff_25_q), .Q(d_ff_29_q[2]));  // open: Qn, preset, reset
endmodule
