// Logisim project assignment1.circ as structural Verilog: 1 circuit, main circuit main
module main (
  input  in_1,
  input  in_2,
  input  in_3,
  input  in_4
);

  wire and_1_out, and_2_out, and_3_out, and_4_out, and_5_out, and_6_out, and_7_out, and_8_out, clock_1_out,
       d_ff_6_q, j_k_ff_1_q, j_k_ff_2_q, j_k_ff_3_q, j_k_ff_4_q, j_k_ff_5_q, j_k_ff_6_q, j_k_ff_7_q,
       j_k_ff_8_q, j_k_ff_9_q, j_k_ff_10_q, j_k_ff_11_q, undriven;
  wire [2:0] d_ff_9_q;
  wire [3:0] d_ff_1_q, d_ff_5_q;

  J_K_Flip_Flop j_k_ff_1 (.J(in_1), .K(in_1), .clk(undriven), .Q(j_k_ff_1_q), .reset(and_3_out));  // open: Qn, preset
  LED led_1 (.in(j_k_ff_1_q));
  D_Flip_Flop d_ff_1 (.D(j_k_ff_1_q), .clk(undriven), .Q(d_ff_1_q[0]));  // open: Qn, preset, reset
  J_K_Flip_Flop j_k_ff_2 (
    .J(j_k_ff_1_q), .K(j_k_ff_1_q), .clk(undriven), .Q(j_k_ff_2_q), .reset(and_3_out));  // open: Qn, preset
  D_Flip_Flop d_ff_2 (.D(j_k_ff_2_q), .clk(undriven), .Q(d_ff_1_q[1]));  // open: Qn, preset, reset
  Hex_Digit_Display hex_digit_display_1 ();  // open: value, dp
  LED led_2 (.in(j_k_ff_2_q));
  and and_1 (and_1_out, j_k_ff_1_q, j_k_ff_2_q);
  J_K_Flip_Flop j_k_ff_3 (
    .J(and_1_out), .K(and_1_out), .clk(undriven), .Q(j_k_ff_3_q), .reset(and_3_out));  // open: Qn, preset
  LED led_3 (.in(j_k_ff_3_q));
  D_Flip_Flop d_ff_3 (.D(j_k_ff_3_q), .clk(undriven), .Q(d_ff_1_q[2]));  // open: Qn, preset, reset
  and and_2 (and_2_out, and_1_out, j_k_ff_3_q);
  J_K_Flip_Flop j_k_ff_4 (
    .J(and_2_out), .K(and_2_out), .clk(undriven), .Q(j_k_ff_4_q), .reset(and_3_out));  // open: Qn, preset
  D_Flip_Flop d_ff_4 (.D(j_k_ff_4_q), .clk(undriven), .Q(d_ff_1_q[3]));  // open: Qn, preset, reset
  LED led_4 (.in(j_k_ff_4_q));
  and and_3 (and_3_out, j_k_ff_2_q, j_k_ff_4_q);
  Hex_Digit_Display hex_digit_display_2 (.value(d_ff_1_q));  // open: dp
  Clock clock_1 (.out(clock_1_out));
  J_K_Flip_Flop j_k_ff_5 (
    .J(in_2), .K(in_2), .clk(clock_1_out), .Q(j_k_ff_5_q), .reset(and_7_out));  // open: Qn, preset
  D_Flip_Flop d_ff_5 (.D(j_k_ff_5_q), .clk(clock_1_out), .Q(d_ff_5_q[0]));  // open: Qn, preset, reset
  D_Flip_Flop d_ff_6 (.D(j_k_ff_10_q), .clk(clock_1_out), .Q(d_ff_6_q));  // open: Qn, preset, reset
  Hex_Digit_Display hex_digit_display_3 (.value({in_4, d_ff_9_q}));  // open: dp
  LED led_5 (.in(j_k_ff_5_q));
  Hex_Digit_Display hex_digit_display_4 (.value(d_ff_5_q));  // open: dp
  J_K_Flip_Flop j_k_ff_6 (
    .J(j_k_ff_5_q), .K(j_k_ff_5_q), .clk(clock_1_out), .Q(j_k_ff_6_q), .reset(and_7_out));  // open: Qn, preset
  D_Flip_Flop d_ff_7 (.D(j_k_ff_6_q), .clk(clock_1_out), .Q(d_ff_5_q[1]));  // open: Qn, preset, reset
  J_K_Flip_Flop j_k_ff_7 (.J(in_3), .K(in_3), .clk(d_ff_6_q), .Q(j_k_ff_7_q), .reset(and_8_out));  // open: Qn, preset
  LED led_6 (.in(j_k_ff_7_q));
  and and_4 (and_4_out, j_k_ff_5_q, j_k_ff_6_q);
  J_K_Flip_Flop j_k_ff_8 (
    .J(and_4_out), .K(and_4_out), .clk(clock_1_out), .Q(j_k_ff_8_q), .reset(and_7_out));  // open: Qn, preset
  LED led_7 (.in(j_k_ff_6_q));
  D_Flip_Flop d_ff_8 (.D(j_k_ff_8_q), .clk(clock_1_out), .Q(d_ff_5_q[2]));  // open: Qn, preset, reset
  J_K_Flip_Flop j_k_ff_9 (
    .J(j_k_ff_7_q), .K(j_k_ff_7_q), .clk(d_ff_6_q), .Q(j_k_ff_9_q), .reset(and_8_out));  // open: Qn, preset
  D_Flip_Flop #(.trigger("falling")) d_ff_9 (
    .D(j_k_ff_7_q), .clk(d_ff_6_q), .Q(d_ff_9_q[0]));  // open: Qn, preset, reset
  LED led_8 (.in(j_k_ff_8_q));
  LED led_9 (.in(j_k_ff_9_q));
  and and_5 (and_5_out, and_4_out, j_k_ff_8_q);
  J_K_Flip_Flop j_k_ff_10 (
    .J(and_5_out), .K(and_5_out), .clk(clock_1_out), .Q(j_k_ff_10_q), .reset(and_7_out));  // open: Qn, preset
  D_Flip_Flop d_ff_10 (.D(j_k_ff_10_q), .clk(clock_1_out), .Q(d_ff_5_q[3]));  // open: Qn, preset, reset
  and and_6 (and_6_out, j_k_ff_7_q, j_k_ff_9_q);
  J_K_Flip_Flop j_k_ff_11 (
    .J(and_6_out), .K(and_6_out), .clk(d_ff_6_q), .Q(j_k_ff_11_q), .reset(and_8_out));  // open: Qn, preset
  D_Flip_Flop #(.trigger("falling")) d_ff_11 (
    .D(j_k_ff_9_q), .clk(d_ff_6_q), .Q(d_ff_9_q[1]));  // open: Qn, preset, reset
  LED led_10 (.in(j_k_ff_10_q));
  LED led_11 (.in(j_k_ff_11_q));
  D_Flip_Flop #(.trigger("falling")) d_ff_12 (
    .D(j_k_ff_11_q), .clk(d_ff_6_q), .Q(d_ff_9_q[2]));  // open: Qn, preset, reset
  and and_7 (and_7_out, j_k_ff_6_q, j_k_ff_10_q);
  and and_8 (and_8_out, j_k_ff_11_q, j_k_ff_9_q);
endmodule
