// Logisim project assing1.circ as structural Verilog: 1 circuit, main circuit main
module main (
  input  in_1,
  input  in_2,
  input  in_3
);

  wire and_1_out, and_2_out, and_3_out, and_4_out, and_5_out, clock_1_out, d_ff_1_q, j_k_ff_1_q, j_k_ff_2_q,
       j_k_ff_3_q, j_k_ff_4_q, j_k_ff_5_q, j_k_ff_6_q, j_k_ff_7_q;
  wire [2:0] d_ff_3_q;
  wire [3:0] d_ff_2_q;

  Clock clock_1 (.out(clock_1_out));
  D_Flip_Flop d_ff_1 (.D(j_k_ff_7_q), .clk(clock_1_out), .Q(d_ff_1_q));  // open: Qn, preset, reset
  J_K_Flip_Flop j_k_ff_1 (
    .J(in_1), .K(in_1), .clk(clock_1_out), .Q(j_k_ff_1_q), .reset(and_5_out));  // open: Qn, preset
  LED led_1 (.in(j_k_ff_1_q));
  D_Flip_Flop d_ff_2 (.D(j_k_ff_1_q), .clk(clock_1_out), .Q(d_ff_2_q[0]));  // open: Qn, preset, reset
  J_K_Flip_Flop j_k_ff_2 (.J(in_2), .K(in_2), .clk(d_ff_1_q), .Q(j_k_ff_2_q), .reset(and_4_out));  // open: Qn, preset
  D_Flip_Flop d_ff_3 (.D(j_k_ff_2_q), .clk(d_ff_1_q), .Q(d_ff_3_q[0]));  // open: Qn, preset, reset
  J_K_Flip_Flop j_k_ff_3 (
    .J(j_k_ff_1_q), .K(j_k_ff_1_q), .clk(clock_1_out), .Q(j_k_ff_3_q), .reset(and_5_out));  // open: Qn, preset
  LED led_2 (.in(j_k_ff_2_q));
  D_Flip_Flop d_ff_4 (.D(j_k_ff_4_q), .clk(d_ff_1_q), .Q(d_ff_3_q[1]));  // open: Qn, preset, reset
  LED led_3 (.in(j_k_ff_3_q));
  D_Flip_Flop d_ff_5 (.D(j_k_ff_3_q), .clk(clock_1_out), .Q(d_ff_2_q[1]));  // open: Qn, preset, reset
  and and_1 (and_1_out, j_k_ff_2_q, j_k_ff_4_q);
  J_K_Flip_Flop j_k_ff_4 (
    .J(j_k_ff_2_q), .K(j_k_ff_2_q), .clk(d_ff_1_q), .Q(j_k_ff_4_q), .reset(and_4_out));  // open: Qn, preset
  and and_2 (and_2_out, j_k_ff_1_q, j_k_ff_3_q);
  J_K_Flip_Flop j_k_ff_5 (
    .J(and_2_out), .K(and_2_out), .clk(clock_1_out), .Q(j_k_ff_5_q), .reset(and_5_out));  // open: Qn, preset
  D_Flip_Flop d_ff_6 (.D(j_k_ff_5_q), .clk(clock_1_out), .Q(d_ff_2_q[2]));  // open: Qn, preset, reset
  J_K_Flip_Flop j_k_ff_6 (
    .J(and_1_out), .K(and_1_out), .clk(d_ff_1_q), .Q(j_k_ff_6_q), .reset(and_4_out));  // open: Qn, preset
  LED led_4 (.in(j_k_ff_4_q));
  D_Flip_Flop d_ff_7 (.D(j_k_ff_6_q), .clk(d_ff_1_q), .Q(d_ff_3_q[2]));  // open: Qn, preset, reset
  and and_3 (and_3_out, and_2_out, j_k_ff_5_q);
  J_K_Flip_Flop j_k_ff_7 (
    .J(and_3_out), .K(and_3_out), .clk(clock_1_out), .Q(j_k_ff_7_q), .reset(and_5_out));  // open: Qn, preset
  LED led_5 (.in(j_k_ff_5_q));
  LED led_6 (.in(j_k_ff_6_q));
  LED led_7 (.in(j_k_ff_7_q));
  D_Flip_Flop d_ff_8 (.D(j_k_ff_7_q), .clk(clock_1_out), .Q(d_ff_2_q[3]));  // open: Qn, preset, reset
  and and_4 (and_4_out, j_k_ff_4_q, j_k_ff_6_q);
  and and_5 (and_5_out, j_k_ff_3_q, j_k_ff_7_q);
  Hex_Digit_Display hex_digit_display_1 (.value({in_3, d_ff_3_q}));  // open: dp
  Hex_Digit_Display hex_digit_display_2 (.value(d_ff_2_q));  // open: dp
  Hex_Digit_Display hex_digit_display_3 ();  // open: value, dp
  Hex_Digit_Display hex_digit_display_4 ();  // open: value, dp
endmodule
