// Logisim project AND.circ as structural Verilog: 1 circuit, main circuit main
module main (
  input  input_1,
  input  input_2
);

  wire and_1_out;

  and and_1 (and_1_out, input_1, input_2);
  LED led_1 (.in(and_1_out));

  // Notes on the sheet:
  //   And Gate
  //   Output
endmodule
