// Logisim project Nandgate.circ as structural Verilog: 1 circuit, main circuit main
module main (
  input  in_1,
  input  in_2
);

  wire nand_1_out;

  not nand_1 (nand_1_out, in_2);  // NAND_Gate
  LED led_1 (.in(nand_1_out));

  // Notes on the sheet:
  //   input 1
  //   input 2
  //   NAND Gate
  //   output
endmodule
