// Logisim project fulladdergate.circ as structural Verilog: 1 circuit, main circuit main
module main (
  input  C_in,
  input  In_1,
  input  in_2
);

  wire and_1_out, and_2_out, or_1_out, xor_1_out, xor_2_out;

  xor xor_1 (xor_1_out, In_1, in_2);
  and and_1 (and_1_out, In_1, in_2);
  xor xor_2 (xor_2_out, C_in, xor_1_out);
  and and_2 (and_2_out, C_in, xor_1_out);
  LED led_1 (.in(xor_2_out));
  or or_1 (or_1_out, and_2_out, and_1_out);
  LED led_2 (.in(or_1_out));

  // Notes on the sheet:
  //   full adder
  //   sum 1
  //   c out 1
endmodule
