// Logisim project notgate.circ as structural Verilog: 1 circuit, main circuit main
module main (
  input  pin
);

  wire not_1_out;

  not not_1 (not_1_out, pin);
  LED led_1 (.in(not_1_out));

  // Notes on the sheet:
  //   Not Gate
  //   output
endmodule
