// Logisim project 4bitadder.circ as structural Verilog: 1 circuit, main circuit main
module main (
  input  input_A,
  input  inputB,
  input  inputA,
  input  input_B,
  input  input_A_2,
  input  inputB_2,
  input  input_A_3,
  input  inputB_3
);

  wire and_1_out, and_2_out, and_3_out, and_4_out, and_5_out, and_6_out, and_7_out, or_1_out, or_2_out,
       or_3_out, xor_1_out, xor_2_out, xor_3_out, xor_4_out, xor_5_out, xor_6_out, xor_7_out;

  xor xor_1 (xor_1_out, inputA, input_B);
  and and_1 (and_1_out, inputA, input_B);
  xor xor_2 (xor_2_out, input_A_2, inputB_2);
  and and_2 (and_2_out, input_A_2, inputB_2);
  xor xor_3 (xor_3_out, input_A_3, inputB_3);
  and and_3 (and_3_out, input_A_3, inputB_3);
  xor xor_4 (xor_4_out, or_3_out, xor_3_out);
  buf and_4 (and_4_out, xor_3_out);  // AND_Gate
  xor xor_5 (xor_5_out, input_A, inputB);
  and and_5 (and_5_out, input_A, input_A);
  xor xor_6 (xor_6_out, and_5_out, xor_1_out);
  and and_6 (and_6_out, and_5_out, xor_1_out);
  xor xor_7 (xor_7_out, or_2_out, xor_2_out);
  and and_7 (and_7_out, or_2_out, xor_2_out);
  LED led_1 (.in(xor_4_out));
  or or_1 (or_1_out, and_4_out, and_3_out);
  LED led_2 (.in(xor_5_out));
  LED led_3 (.in(xor_6_out));
  or or_2 (or_2_out, and_6_out, and_1_out);
  LED led_4 (.in(xor_7_out));
  or or_3 (or_3_out, and_7_out, and_2_out);
  LED led_5 (.in(or_1_out));

  // Notes on the sheet:
  //   4bit adder
  //   out 0
  //   out 3
  //   out 1
  //   out 2 
  //   carryout (overflow)
endmodule
