// Logisim project Assignment_1_Digital_Alarm_clock.circ as structural Verilog: 1 circuit, main circuit main
module main (
  input  s1,
  input  s2,
  input  s3,
  input  s4,
  input  SETTING_TIME,
  input  in_6,
  input  in_7,
  input  in_8,
  input  in_9
);

  wire and_1_out, and_2_out, and_3_out, and_4_out, and_5_out, and_6_out, and_7_out, and_8_out, and_9_out,
       and_10_out, and_11_out, and_12_out, and_13_out, and_14_out, and_15_out, and_16_out, and_17_out,
       and_18_out, and_19_out, button_1_out, button_2_out, clock_1_out, d_ff_7_q, d_ff_7_qn, d_ff_8_qn,
       d_ff_17_q, d_ff_18_qn, j_k_ff_1_q, j_k_ff_2_q, j_k_ff_3_q, j_k_ff_4_q, j_k_ff_5_q, j_k_ff_6_q,
       j_k_ff_7_q, j_k_ff_8_q, j_k_ff_9_q, j_k_ff_10_q, j_k_ff_11_q, j_k_ff_12_q, j_k_ff_13_q, j_k_ff_14_q,
       j_k_ff_15_q, or_1_out, or_2_out, or_3_out, xor_1_out, xor_2_out;
  wire [2:0] d_ff_1_q, d_ff_2_q;
  wire [3:0] d_ff_9_q, d_ff_11_q;

  Button button_1 (.out(button_1_out));
  Clock clock_1 (.out(clock_1_out));
  Button button_2 (.out(button_2_out));
  and and_1 (and_1_out, button_1_out, SETTING_TIME);
  or or_1 (or_1_out, SETTING_TIME, clock_1_out);
  and and_2 (and_2_out, SETTING_TIME, button_2_out);
  xor xor_1 (xor_1_out, d_ff_18_qn, and_2_out);
  xor xor_2 (xor_2_out, and_1_out, or_1_out);
  and and_3 (and_3_out, j_k_ff_1_q, j_k_ff_5_q);
  J_K_Flip_Flop #(.trigger("falling")) j_k_ff_1 (
    .J(s2), .K(s2), .clk(d_ff_7_qn), .Q(j_k_ff_1_q), .reset(and_5_out));  // open: Qn, preset
  LED led_1 (.in(j_k_ff_1_q));
  D_Flip_Flop d_ff_1 (.D(j_k_ff_1_q), .clk(d_ff_7_qn), .Q(d_ff_1_q[0]));  // open: Qn, preset, reset
  J_K_Flip_Flop #(.trigger("falling")) j_k_ff_2 (
    .J(s4), .K(s4), .clk(d_ff_8_qn), .Q(j_k_ff_2_q), .reset(or_2_out));  // open: Qn, preset
  or or_2 (or_2_out, and_7_out, j_k_ff_4_q);
  LED led_2 (.in(j_k_ff_2_q));
  D_Flip_Flop d_ff_2 (.D(j_k_ff_2_q), .clk(d_ff_8_qn), .Q(d_ff_2_q[0]), .reset(d_ff_17_q));  // open: Qn, preset
  and and_4 (and_4_out, j_k_ff_1_q, j_k_ff_3_q);
  J_K_Flip_Flop #(.trigger("falling")) j_k_ff_3 (
    .J(j_k_ff_1_q), .K(j_k_ff_1_q), .clk(d_ff_7_qn), .Q(j_k_ff_3_q), .reset(and_5_out));  // open: Qn, preset
  D_Flip_Flop d_ff_3 (.D(j_k_ff_3_q), .clk(d_ff_7_qn), .Q(d_ff_1_q[1]));  // open: Qn, preset, reset
  J_K_Flip_Flop #(.trigger("falling")) j_k_ff_4 (
    .J(j_k_ff_2_q), .K(j_k_ff_2_q), .clk(d_ff_8_qn), .Q(j_k_ff_4_q), .reset(j_k_ff_4_q));  // open: Qn, preset
  D_Flip_Flop d_ff_4 (.D(j_k_ff_4_q), .clk(d_ff_8_qn), .Q(d_ff_2_q[1]));  // open: Qn, preset, reset
  J_K_Flip_Flop #(.trigger("falling")) j_k_ff_5 (
    .J(and_4_out), .K(and_4_out), .clk(d_ff_7_qn), .Q(j_k_ff_5_q), .reset(and_5_out));  // open: Qn, preset
  and and_5 (and_5_out, j_k_ff_3_q, j_k_ff_5_q);
  LED led_3 (.in(j_k_ff_3_q));
  D_Flip_Flop d_ff_5 (.D(j_k_ff_5_q), .clk(d_ff_7_qn), .Q(d_ff_1_q[2]));  // open: Qn, preset, reset
  and and_6 (and_6_out, j_k_ff_2_q, j_k_ff_4_q);
  J_K_Flip_Flop #(.trigger("falling")) j_k_ff_6 (
    .J(and_6_out), .K(and_6_out), .clk(d_ff_8_qn), .Q(j_k_ff_6_q), .reset(j_k_ff_4_q));  // open: Qn, preset
  LED led_4 (.in(j_k_ff_4_q));
  D_Flip_Flop d_ff_6 (.D(j_k_ff_6_q), .clk(d_ff_8_qn), .Q(d_ff_2_q[2]));  // open: Qn, preset, reset
  Hex_Digit_Display hex_digit_display_1 (.value({in_8, d_ff_2_q}));  // open: dp
  LED led_5 (.in(j_k_ff_5_q));
  LED led_6 (.in(j_k_ff_6_q));
  and and_7 (and_7_out, j_k_ff_2_q, and_10_out);
  Hex_Digit_Display hex_digit_display_2 (.value(d_ff_11_q));  // open: dp
  Hex_Digit_Display hex_digit_display_3 (.value({in_6, d_ff_1_q}));  // open: dp
  D_Flip_Flop d_ff_7 (.D(and_8_out), .clk(xor_2_out), .Q(d_ff_7_q), .Qn(d_ff_7_qn));  // open: preset, reset
  LED led_7 (.in(j_k_ff_7_q));
  LED led_8 ();  // open: in
  Hex_Digit_Display hex_digit_display_4 (.value(d_ff_9_q));  // open: dp
  J_K_Flip_Flop j_k_ff_7 (.J(and_9_out), .K(and_9_out), .clk(xor_1_out), .Q(j_k_ff_7_q));  // open: Qn, preset, reset
  D_Flip_Flop d_ff_8 (.D(and_12_out), .clk(xor_1_out), .Qn(d_ff_8_qn));  // open: Q, preset, reset
  and and_8 (and_8_out, j_k_ff_12_q, j_k_ff_8_q);
  J_K_Flip_Flop #(.trigger("falling")) j_k_ff_8 (
    .J(s1), .K(s1), .clk(xor_2_out), .Q(j_k_ff_8_q), .reset(and_15_out));  // open: Qn, preset
  LED led_9 (.in(j_k_ff_8_q));
  D_Flip_Flop d_ff_9 (.D(j_k_ff_8_q), .clk(xor_2_out), .Q(d_ff_9_q[0]));  // open: Qn, preset, reset
  and and_9 (and_9_out, j_k_ff_2_q, j_k_ff_13_q);
  and and_10 (and_10_out, j_k_ff_10_q, j_k_ff_13_q);
  and and_11 (and_11_out, j_k_ff_8_q, j_k_ff_9_q);
  J_K_Flip_Flop #(.trigger("falling")) j_k_ff_9 (
    .J(j_k_ff_8_q), .K(j_k_ff_8_q), .clk(xor_2_out), .Q(j_k_ff_9_q), .reset(and_15_out));  // open: Qn, preset
  D_Flip_Flop d_ff_10 (.D(j_k_ff_9_q), .clk(xor_2_out), .Q(d_ff_9_q[1]));  // open: Qn, preset, reset
  J_K_Flip_Flop #(.trigger("falling")) j_k_ff_10 (
    .J(s3), .K(s3), .clk(xor_1_out), .Q(j_k_ff_10_q), .reset(and_17_out));  // open: Qn, preset
  and and_12 (and_12_out, j_k_ff_15_q, j_k_ff_10_q);
  D_Flip_Flop d_ff_11 (.D(j_k_ff_10_q), .clk(xor_1_out), .Q(d_ff_11_q[0]));  // open: Qn, preset, reset
  J_K_Flip_Flop #(.trigger("falling")) j_k_ff_11 (
    .J(and_11_out), .K(and_11_out), .clk(xor_2_out), .Q(j_k_ff_11_q), .reset(and_15_out));  // open: Qn, preset
  LED led_10 (.in(j_k_ff_9_q));
  D_Flip_Flop d_ff_12 (.D(j_k_ff_11_q), .clk(xor_2_out), .Q(d_ff_9_q[2]));  // open: Qn, preset, reset
  LED led_11 (.in(j_k_ff_10_q));
  and and_13 (and_13_out, and_11_out, j_k_ff_11_q);
  J_K_Flip_Flop #(.trigger("falling")) j_k_ff_12 (
    .J(and_13_out), .K(and_13_out), .clk(xor_2_out), .Q(j_k_ff_12_q), .reset(and_15_out));  // open: Qn, preset
  LED led_12 (.in(j_k_ff_11_q));
  D_Flip_Flop d_ff_13 (.D(j_k_ff_12_q), .clk(xor_2_out), .Q(d_ff_9_q[3]));  // open: Qn, preset, reset
  and and_14 (and_14_out, j_k_ff_10_q, j_k_ff_13_q);
  J_K_Flip_Flop #(.trigger("falling")) j_k_ff_13 (
    .J(j_k_ff_10_q), .K(j_k_ff_10_q), .clk(xor_1_out), .Q(j_k_ff_13_q), .reset(or_3_out));  // open: Qn, preset
  LED led_13 (.in(j_k_ff_13_q));
  D_Flip_Flop d_ff_14 (.D(j_k_ff_13_q), .clk(xor_1_out), .Q(d_ff_11_q[1]));  // open: Qn, preset, reset
  or or_3 (or_3_out, and_7_out, and_17_out);
  LED led_14 (.in(j_k_ff_12_q));
  J_K_Flip_Flop #(.trigger("falling")) j_k_ff_14 (
    .J(and_14_out), .K(and_14_out), .clk(xor_1_out), .Q(j_k_ff_14_q), .reset(and_17_out));  // open: Qn, preset
  D_Flip_Flop d_ff_15 (.D(j_k_ff_14_q), .clk(xor_1_out), .Q(d_ff_11_q[2]));  // open: Qn, preset, reset
  and and_15 (and_15_out, j_k_ff_12_q, j_k_ff_9_q);
  and and_16 (and_16_out, and_14_out, j_k_ff_14_q);
  J_K_Flip_Flop #(.trigger("falling")) j_k_ff_15 (
    .J(and_16_out), .K(and_16_out), .clk(xor_1_out), .Q(j_k_ff_15_q), .reset(and_17_out));  // open: Qn, preset
  LED led_15 (.in(j_k_ff_14_q));
  D_Flip_Flop d_ff_16 (.D(j_k_ff_15_q), .clk(xor_1_out), .Q(d_ff_11_q[3]));  // open: Qn, preset, reset
  LED led_16 (.in(j_k_ff_15_q));
  and and_17 (and_17_out, j_k_ff_15_q, j_k_ff_13_q);
  and and_18 (and_18_out, and_8_out, and_3_out);
  and and_19 (and_19_out, d_ff_11_q[1], j_k_ff_10_q);
  D_Flip_Flop d_ff_17 (.D(and_19_out), .clk(xor_1_out), .Q(d_ff_17_q));  // open: Qn, preset, reset
  D_Flip_Flop d_ff_18 (.D(and_18_out), .clk(xor_2_out), .Qn(d_ff_18_qn));  // open: Q, preset, reset

  // Notes on the sheet:
  //   Switches for the clock
  //   ClOCK
  //   COS 10004 Assignment 1 Digital Alarm Clock 
  //   A.M
  //   P.M
  //   NAME: Nur E Siam
  //   STUDENT ID: 103842784
endmodule
